// Logisim project RRISC.circ as structural Verilog: 4 circuits, main circuit main
module main (
);

  wire ACC_OUT_IS_JMP, BSYS_CLK_out, dipswitch_1_p1, EX, INST_ALU, INST_MEM, INSTF, RST, WB;
  wire [3:0] ACC_OUT_RX_WB, controlled_buffer_2_out, controlled_buffer_4_out;
  wire [7:0] ALU_OUT_RESULT, ALU_RESULT_q, controlled_buffer_5_out, IR_q, R0_ACC, ram_1_dout,
       regs_1_out_regdata;
  wire [15:0] adder_1_out, MEMADDR, multiplexer_1_out, PC_q, REGS_OUT_MEM;

  RAM #(.addrWidth(16), .trigger("high")) ram_1 (.addr(MEMADDR), .we(1'b0), .oe(1'b1), .dout(ram_1_dout));  // open: din
  Multiplexer #(.enable("false"), .width(16)) multiplexer_1 (
    .in0(adder_1_out), .in1(REGS_OUT_MEM), .out(multiplexer_1_out), .sel(ACC_OUT_IS_JMP));
  Register #(.width(16)) PC (.D(multiplexer_1_out), .en(1'b1), .clk(EX), .Q(PC_q), .clr(RST));
  Adder #(.width(16)) adder_1 (.a(PC_q), .b(16'h1), .out(adder_1_out));  // open: cin, cout
  // Probe on ram_1_dout
  assign MEMADDR = INSTF ? PC_q : 16'bz;  // Controlled_Buffer controlled_buffer_1
  Register #(.trigger("high")) IR (.D(ram_1_dout), .en(1'b1), .clk(INSTF), .Q(IR_q), .clr(RST));
  // DipSwitch #(.number(2)) dipswitch_1: pin names not known; wires that end beside it: dipswitch_1_p1, ALU_OUT_RESULT
  Register ALU_RESULT (.D(ALU_OUT_RESULT), .en(1'b1), .clk(WB), .Q(ALU_RESULT_q), .clr(RST));
  Button BSYS_CLK (.out(BSYS_CLK_out));
  Button BRST (.out(RST));
  // Probe on IR_q
  assign controlled_buffer_2_out = EX ? IR_q[3:0] : 4'bz;  // Controlled_Buffer controlled_buffer_2
  assign controlled_buffer_2_out = WB ? ACC_OUT_RX_WB : 4'bz;  // Controlled_Buffer controlled_buffer_3
  assign controlled_buffer_4_out = INST_ALU ? controlled_buffer_2_out : 4'bz;  // Controlled_Buffer controlled_buffer_4
  assign controlled_buffer_5_out = INST_ALU ? ALU_RESULT_q : 8'bz;  // Controlled_Buffer controlled_buffer_5
  nand nand_1 (INST_ALU, IR_q[7], IR_q[6]);
  and u_INST_MEM (INST_MEM, IR_q[7], IR_q[6], IR_q[5]);
  Controller controller_1 (.STEP(dipswitch_1_p1), .CLK(BSYS_CLK_out), .RST(RST), .INSTF(INSTF), .EX(EX), .WB(WB));
  // Probe on R0_ACC
  REGS regs_1 (
    .RST(RST), .Data(controlled_buffer_5_out), .CLK(WB), .Write(WB), .Rx(controlled_buffer_4_out),
    .OUT_R0_ACC(R0_ACC), .OUT_REGDATA(regs_1_out_regdata), .OUT_MEM(REGS_OUT_MEM));  // open: OUT_MEMIO
  // Probe on ALU_OUT_RESULT
  ALU alu_1 (
    .REGDATA(regs_1_out_regdata), .IN_ACC(R0_ACC), .IN_IMMEDIATE(IR_q[3:0]), .OPCODE(IR_q[7:4]),
    .OUT_RESULT(ALU_OUT_RESULT), .OUT_IS_JMP(ACC_OUT_IS_JMP), .OUT_RX_WB(ACC_OUT_RX_WB));
  // Probe on ACC_OUT_RX_WB
  assign MEMADDR = WB ? REGS_OUT_MEM : 16'bz;  // Controlled_Buffer controlled_buffer_6
  assign MEMADDR = EX ? REGS_OUT_MEM : 16'bz;  // Controlled_Buffer controlled_buffer_7

  // Notes on the sheet:
  //   Does  one cycle per press
endmodule

module ALU (
  input  [7:0] REGDATA,
  input  [7:0] IN_ACC,
  input  [3:0] IN_IMMEDIATE,
  input  [3:0] OPCODE,
  output [7:0] OUT_RESULT,
  output OUT_IS_JMP,
  output [3:0] OUT_RX_WB
);

  wire comparator_1_eq, INST_MOV_out, not_1_out, not_2_out;
  wire [7:0] adder_1_out, and_2_out, bit_extender_1_out, nand_1_out, REGORIMM, shifter_1_out;
  wire [7:7] NotEqZero;

  assign bit_extender_1_out = {{4{1'b0}}, IN_IMMEDIATE};  // Bit_Extender bit_extender_1
  assign REGORIMM = not_1_out ? bit_extender_1_out : 8'bz;  // Controlled_Buffer controlled_buffer_1
  not not_1 (not_1_out, OPCODE[0]);
  assign REGORIMM = OPCODE[0] ? REGDATA : 8'bz;  // Controlled_Buffer controlled_buffer_2
  and and_1 (NotEqZero[7], REGORIMM[0], REGORIMM[1], REGORIMM[2], REGORIMM[3], REGORIMM[4], REGORIMM[5], REGORIMM[6], REGORIMM[7]);
  assign OUT_RX_WB = INST_MOV_out ? IN_IMMEDIATE : 4'bz;  // Controlled_Buffer controlled_buffer_3
  and INST_MOV (INST_MOV_out, OPCODE[3], ~OPCODE[2], ~OPCODE[1], ~OPCODE[0]);  // AND_Gate
  assign OUT_RX_WB = not_2_out ? 4'b0000 : 4'bz;  // Controlled_Buffer controlled_buffer_4
  not not_2 (not_2_out, INST_MOV_out);
  Adder adder_1 (.a(IN_ACC), .b(REGORIMM), .out(adder_1_out));  // open: cin, cout
  assign and_2_out = IN_ACC & REGORIMM;  // AND_Gate and_2, 8 bits wide
  Shifter shifter_1 (.in(IN_ACC), .\dist (REGORIMM[2:0]), .out(shifter_1_out));
  assign nand_1_out = ~(IN_ACC & REGORIMM);  // NAND_Gate nand_1, 8 bits wide
  Comparator comparator_1 (.a(REGORIMM), .b(IN_ACC), .eq(comparator_1_eq));  // open: gt, lt
  and and_3 (OUT_IS_JMP, OPCODE[3], OPCODE[2], ~OPCODE[1]);  // AND_Gate
  Multiplexer #(.enable("false"), .select(4), .width(8)) multiplexer_1 (
    .in0(adder_1_out), .in1(adder_1_out), .in2(and_2_out), .in3(and_2_out), .in4(shifter_1_out),
    .in5(shifter_1_out), .in6(nand_1_out), .in7(nand_1_out), .in8(IN_ACC), .out(OUT_RESULT), .sel(OPCODE));  // open: in9, in10, in11, in12, in13, in14, in15

  // Other names for the same wires on the sheet: IMMEDIATE[3:0] = IN_IMMEDIATE; NotEqZero[6:0] = {7{NotEqZero[7]}}

  // Notes on the sheet:
  //   Data is register or immediate
  //   For MOV instruction (IF MOV (DST=IMM) ELSE (DST=ACC)
  //   TODO add conditional jump
endmodule

module REGS (
  input  RST,
  input  [7:0] Data,
  input  CLK,
  input  Write,
  input  [3:0] Rx,
  output [7:0] OUT_R0_ACC,
  output [7:0] OUT_REGDATA,
  output [7:0] OUT_MEMIO,
  output [15:0] OUT_MEM
);

  wire demultiplexer_1_out0, demultiplexer_1_out1, demultiplexer_1_out2, demultiplexer_1_out3,
       demultiplexer_1_out4, demultiplexer_1_out5, demultiplexer_1_out6, demultiplexer_1_out7,
       demultiplexer_1_out8, demultiplexer_1_out9, demultiplexer_1_out10, demultiplexer_1_out11,
       demultiplexer_1_out12, demultiplexer_1_out13, demultiplexer_1_out14, demultiplexer_1_out15;
  wire [7:0] R1_q, R2_q, R3_q, R4_q, R5_q, R6_q, R7_q, R8_q, R9_q, R10_q, R11_q, R12_q;

  Demultiplexer #(.enable("false"), .select(4)) demultiplexer_1 (
    .out0(demultiplexer_1_out0), .out1(demultiplexer_1_out1), .out2(demultiplexer_1_out2),
    .out3(demultiplexer_1_out3), .out4(demultiplexer_1_out4), .out5(demultiplexer_1_out5),
    .out6(demultiplexer_1_out6), .out7(demultiplexer_1_out7), .out8(demultiplexer_1_out8),
    .out9(demultiplexer_1_out9), .out10(demultiplexer_1_out10), .out11(demultiplexer_1_out11),
    .out12(demultiplexer_1_out12), .out13(demultiplexer_1_out13), .out14(demultiplexer_1_out14),
    .out15(demultiplexer_1_out15), .in(Write), .sel(Rx));
  Register #(.trigger("high")) R0_ACC (.D(Data), .en(demultiplexer_1_out0), .clk(CLK), .Q(OUT_R0_ACC), .clr(RST));
  Register #(.trigger("high")) R1 (.D(Data), .en(demultiplexer_1_out1), .clk(CLK), .Q(R1_q), .clr(RST));
  Register #(.trigger("high")) R2 (.D(Data), .en(demultiplexer_1_out2), .clk(CLK), .Q(R2_q), .clr(RST));
  Register #(.trigger("high")) R3 (.D(Data), .en(demultiplexer_1_out3), .clk(CLK), .Q(R3_q), .clr(RST));
  Register #(.trigger("high")) R4 (.D(Data), .en(demultiplexer_1_out4), .clk(CLK), .Q(R4_q), .clr(RST));
  Register #(.trigger("high")) R5 (.D(Data), .en(demultiplexer_1_out5), .clk(CLK), .Q(R5_q), .clr(RST));
  Register #(.trigger("high")) R6 (.D(Data), .en(demultiplexer_1_out6), .clk(CLK), .Q(R6_q), .clr(RST));
  Register #(.trigger("high")) R7 (.D(Data), .en(demultiplexer_1_out7), .clk(CLK), .Q(R7_q), .clr(RST));
  Register #(.trigger("high")) R8 (.D(Data), .en(demultiplexer_1_out8), .clk(CLK), .Q(R8_q), .clr(RST));
  Register #(.trigger("high")) R9 (.D(Data), .en(demultiplexer_1_out9), .clk(CLK), .Q(R9_q), .clr(RST));
  Register #(.trigger("high")) R10 (.D(Data), .en(demultiplexer_1_out10), .clk(CLK), .Q(R10_q), .clr(RST));
  Register #(.trigger("high")) R11 (.D(Data), .en(demultiplexer_1_out11), .clk(CLK), .Q(R11_q), .clr(RST));
  Register #(.trigger("high")) R12 (.D(Data), .en(demultiplexer_1_out12), .clk(CLK), .Q(R12_q), .clr(RST));
  Register #(.trigger("high")) R13_MEMIO (.D(Data), .en(demultiplexer_1_out13), .clk(CLK), .Q(OUT_MEMIO), .clr(RST));
  Register #(.trigger("high")) R14_MEMH (.D(Data), .en(demultiplexer_1_out14), .clk(CLK), .Q(OUT_MEM[15:8]), .clr(RST));
  Register #(.trigger("high")) R15_MEML (.D(Data), .en(demultiplexer_1_out15), .clk(CLK), .Q(OUT_MEM[7:0]), .clr(RST));
  Multiplexer #(.enable("false"), .select(4), .width(8)) multiplexer_1 (
    .in0(OUT_R0_ACC), .in1(R1_q), .in2(R2_q), .in3(R3_q), .in4(R4_q), .in5(R5_q), .in6(R6_q), .in7(R7_q),
    .in8(R8_q), .in9(R9_q), .in10(R10_q), .in11(R11_q), .in12(R12_q), .in13(OUT_MEMIO), .in14(OUT_MEM[15:8]),
    .in15(OUT_MEM[7:0]), .out(OUT_REGDATA), .sel(Rx));

  // Notes on the sheet:
  //   NOTE: Registers MUST have WriteEn and OutEn
  //   No mux could have 128 inputs
endmodule

module Controller (
  input  STEP,
  input  CLK,
  input  RST,
  output INSTF,
  output EX,
  output WB
);

  wire and_1_out, clock_1_out, demultiplexer_1_out3, or_1_out, or_2_out, or_3_out;
  wire [2:0] adder_1_out, CTR_q;

  or or_1 (or_1_out, ~INSTF, CLK);  // OR_Gate
  or or_2 (or_2_out, RST, demultiplexer_1_out3);
  Clock clock_1 (.out(clock_1_out));
  or or_3 (or_3_out, and_1_out, CLK);
  and and_1 (and_1_out, clock_1_out, or_1_out, STEP);
  Register #(.width(3)) CTR (.D(adder_1_out), .en(1'b1), .clk(or_3_out), .Q(CTR_q), .clr(or_2_out));
  Adder #(.width(3)) adder_1 (.a(CTR_q), .b(3'b001), .out(adder_1_out));  // open: cin, cout
  Demultiplexer #(.enable("false"), .select(3)) demultiplexer_1 (
    .out0(INSTF), .out1(EX), .out2(WB), .out3(demultiplexer_1_out3), .in(1'b1), .sel(CTR_q));  // open: out4, out5, out6, out7

  // Notes on the sheet:
  //   This is mostly just a ring counter for the pipeline
endmodule
